// Logisim project ESDES.circ as structural Verilog: 15 circuits, main circuit main
module main (
  input  [7:0] Nonce,
  input  [9:0] key,
  input  Reset,
  input  [7:0] Plaintext,
  output [7:0] cipher
);

  wire clock_1_out, or_8_1_out_2;
  wire [7:0] dff_8_1_out_4, dff_8_2_out_4, dff_8_3_out_4, dff_8_4_out_4, ESDES_output_bus_2,
       multiplexer_1_out;

  Clock clock_1 (.out(clock_1_out));
  Multiplexer #(.width(8)) multiplexer_1 (
    .in0(Nonce), .in1(dff_8_3_out_4), .out(multiplexer_1_out), .sel(or_8_1_out_2));
  or_8 or_8_1 (.in_1(dff_8_3_out_4), .out_2(or_8_1_out_2));
  DFF_8 dff_8_1 (.in_1(Plaintext), .in_2(clock_1_out), .in_3(Reset), .out_4(dff_8_1_out_4));
  DFF_8 dff_8_2 (.in_1(multiplexer_1_out), .in_2(clock_1_out), .in_3(Reset), .out_4(dff_8_2_out_4));
  SDES ESDES (.Input_bus_1(dff_8_2_out_4), .Input_bus_2(key), .Output_bus_2(ESDES_output_bus_2));
  DFF_8 dff_8_3 (.in_1(ESDES_output_bus_2), .in_2(clock_1_out), .in_3(Reset), .out_4(dff_8_3_out_4));
  DFF_8 dff_8_4 (.in_1(dff_8_1_out_4), .in_2(clock_1_out), .in_3(Reset), .out_4(dff_8_4_out_4));
  assign cipher = dff_8_3_out_4 ^ dff_8_4_out_4;  // XOR_Gate xor_1, 8 bits wide
endmodule

module Key1 (
  input  Input_1,
  input  Input_2,
  input  Input_3,
  input  Input_4,
  input  Input_5,
  input  Input_6,
  input  Input_7,
  input  Input_8,
  input  Input_9,
  input  Input_10,
  output [7:0] Output_bus_1
);


  assign Output_bus_1 = {Input_1, Input_7, Input_9, Input_4, Input_8, Input_3, Input_10, Input_6};
  // also tied to GND on the sheet: {Input_2, Input_5}
endmodule

module Key2 (
  input  Input_1,
  input  Input_2,
  input  Input_3,
  input  Input_4,
  input  Input_5,
  input  Input_6,
  input  Input_7,
  input  Input_8,
  input  Input_9,
  input  Input_10,
  output [7:0] Output_bus_1
);


  assign Output_bus_1 = {Input_8, Input_3, Input_6, Input_5, Input_10, Input_2, Input_9, Input_1};
  // also tied to GND on the sheet: {Input_4, Input_7}
endmodule

module S0 (
  input  [3:0] Input_bus_1,
  output [1:0] Output_bus_1
);

  wire and_1_out, and_2_out, and_3_out, and_4_out, and_5_out, and_6_out, and_7_out, and_8_out, and_9_out,
       and_10_out, and_11_out, and_12_out, and_13_out, and_14_out, and_15_out, and_16_out, not_1_out,
       not_2_out, not_3_out, not_4_out, or_1_out, or_2_out, or_3_out, or_4_out, or_5_out;

  not not_1 (not_1_out, Input_bus_1[3]);
  not not_2 (not_2_out, Input_bus_1[2]);
  not not_3 (not_3_out, Input_bus_1[1]);
  not not_4 (not_4_out, Input_bus_1[0]);
  and and_1 (and_1_out, not_1_out, not_2_out);
  and and_2 (and_2_out, and_1_out, Input_bus_1[0]);
  and and_3 (and_3_out, not_1_out, Input_bus_1[2]);
  and and_4 (and_4_out, and_3_out, not_4_out);
  and and_5 (and_5_out, Input_bus_1[3], Input_bus_1[1]);
  and and_6 (and_6_out, Input_bus_1[3], not_3_out);
  and and_7 (and_7_out, Input_bus_1[3], Input_bus_1[2]);
  and and_8 (and_8_out, not_1_out, not_3_out);
  and and_9 (and_9_out, Input_bus_1[3], not_2_out);
  and and_10 (and_10_out, and_9_out, Input_bus_1[0]);
  and and_11 (and_11_out, Input_bus_1[3], Input_bus_1[2]);
  and and_12 (and_12_out, and_11_out, not_4_out);
  and and_13 (and_13_out, not_3_out, Input_bus_1[0]);
  or or_1 (or_1_out, and_2_out, and_4_out);
  and and_14 (and_14_out, and_5_out, not_4_out);
  and and_15 (and_15_out, and_6_out, Input_bus_1[0]);
  and and_16 (and_16_out, and_7_out, Input_bus_1[0]);
  or or_2 (or_2_out, and_8_out, and_10_out);
  or or_3 (or_3_out, and_12_out, and_13_out);
  or or_4 (or_4_out, or_1_out, and_14_out);
  or or_5 (or_5_out, and_15_out, and_16_out);
  or or_6 (Output_bus_1[0], or_2_out, or_3_out);
  or or_7 (Output_bus_1[1], or_4_out, or_5_out);
endmodule

module S1 (
  input  [3:0] Input_bus_1,
  output [1:0] Output_bus_1
);

  wire and_1_out, and_2_out, and_3_out, and_4_out, and_5_out, and_6_out, and_7_out, and_8_out, and_9_out,
       and_10_out, and_11_out, and_12_out, and_13_out, and_14_out, and_15_out, and_16_out, not_1_out,
       not_2_out, not_3_out, not_4_out, or_1_out, or_2_out, or_3_out, or_4_out;

  not not_1 (not_1_out, Input_bus_1[3]);
  not not_2 (not_2_out, Input_bus_1[2]);
  not not_3 (not_3_out, Input_bus_1[1]);
  not not_4 (not_4_out, Input_bus_1[0]);
  and and_1 (and_1_out, not_2_out, not_3_out);
  and and_2 (and_2_out, and_1_out, Input_bus_1[0]);
  and and_3 (and_3_out, not_1_out, Input_bus_1[2]);
  and and_4 (and_4_out, and_3_out, not_4_out);
  and and_5 (and_5_out, Input_bus_1[3], not_2_out);
  and and_6 (and_6_out, and_5_out, not_3_out);
  and and_7 (and_7_out, Input_bus_1[2], Input_bus_1[1]);
  and and_8 (and_8_out, and_7_out, Input_bus_1[0]);
  and and_9 (and_9_out, not_1_out, Input_bus_1[1]);
  and and_10 (and_10_out, and_9_out, not_4_out);
  and and_11 (and_11_out, not_1_out, Input_bus_1[2]);
  and and_12 (and_12_out, and_11_out, Input_bus_1[0]);
  and and_13 (and_13_out, Input_bus_1[3], not_3_out);
  and and_14 (and_14_out, and_13_out, not_4_out);
  and and_15 (and_15_out, Input_bus_1[3], Input_bus_1[1]);
  and and_16 (and_16_out, and_15_out, Input_bus_1[0]);
  or or_1 (or_1_out, and_2_out, and_4_out);
  or or_2 (or_2_out, and_6_out, and_8_out);
  or or_3 (or_3_out, and_10_out, and_12_out);
  or or_4 (or_4_out, and_14_out, and_16_out);
  or or_5 (Output_bus_1[1], or_1_out, or_2_out);
  or or_6 (Output_bus_1[0], or_3_out, or_4_out);
endmodule

module IP (
  input  [7:0] Input_bus_1,
  output [7:0] Output_bus_1
);


  assign Output_bus_1 = {Input_bus_1[6], Input_bus_1[2], Input_bus_1[5], Input_bus_1[7], Input_bus_1[4], Input_bus_1[0], Input_bus_1[3], Input_bus_1[1]};
endmodule

module EP (
  input  Input_1,
  input  Input_2,
  input  Input_3,
  input  Input_4,
  output [7:0] Output_bus_1
);


  assign Output_bus_1 = {Input_1, Input_4, Input_3, Input_2, Input_3, Input_2, Input_1, Input_4};
endmodule

module P4 (
  input  [3:0] Input_bus_1,
  output [3:0] Output_bus_1
);


  assign Output_bus_1 = {Input_bus_1[2], Input_bus_1[0], Input_bus_1[1], Input_bus_1[3]};
endmodule

module IP_inv (
  input  [7:0] Input_bus_1,
  output [7:0] Output_bus_1
);


  assign Output_bus_1 = {Input_bus_1[4], Input_bus_1[7], Input_bus_1[5], Input_bus_1[3], Input_bus_1[1], Input_bus_1[6], Input_bus_1[0], Input_bus_1[2]};
endmodule

module P10 (
  input  [9:0] a,
  output [9:0] b
);


  assign b = {a[7], a[5], a[8], a[3], a[6], a[0], a[9], a[1], a[2], a[4]};
endmodule

module Compliment (
  input  [7:0] Input_bus_1,
  output [7:0] Output_bus_1
);

  not not_1 (Output_bus_1[7], Input_bus_1[7]);
  not not_2 (Output_bus_1[6], Input_bus_1[6]);
  not not_3 (Output_bus_1[5], Input_bus_1[5]);
  not not_4 (Output_bus_1[4], Input_bus_1[4]);
  not not_5 (Output_bus_1[3], Input_bus_1[3]);
  not not_6 (Output_bus_1[2], Input_bus_1[2]);
  not not_7 (Output_bus_1[1], Input_bus_1[1]);
  not not_8 (Output_bus_1[0], Input_bus_1[0]);
endmodule

module Compliment_10 (
  input  [9:0] Input_bus_1,
  output [9:0] Output_bus_1
);

  not not_1 (Output_bus_1[9], Input_bus_1[9]);
  not not_2 (Output_bus_1[8], Input_bus_1[8]);
  not not_3 (Output_bus_1[7], Input_bus_1[7]);
  not not_4 (Output_bus_1[6], Input_bus_1[6]);
  not not_5 (Output_bus_1[5], Input_bus_1[5]);
  not not_6 (Output_bus_1[4], Input_bus_1[4]);
  not not_7 (Output_bus_1[3], Input_bus_1[3]);
  not not_8 (Output_bus_1[2], Input_bus_1[2]);
  not not_9 (Output_bus_1[1], Input_bus_1[1]);
  not not_10 (Output_bus_1[0], Input_bus_1[0]);
endmodule

module SDES (
  input  [7:0] Input_bus_1,
  input  [9:0] Input_bus_2,
  output [7:0] Output_bus_2
);

  wire [1:0] S0_1_output_bus_1, S0_2_output_bus_1, S1_1_output_bus_1, S1_2_output_bus_1;
  wire [3:0] IP_1_output_bus_1, IP_1_output_bus_1_2, P4_1_output_bus_1, P4_2_output_bus_1, xor_2_out,
       xor_4_out;
  wire [6:3] Compliment_10_1_output_bus_1;
  wire [7:0] Compliment_1_output_bus_1, Compliment_10_1_output_bus_1_2, EP_1_output_bus_1, EP_2_output_bus_1,
       IP_inv_1_output_bus_1, xor_1_out, xor_3_out;

  Compliment Compliment_1 (.Input_bus_1(Input_bus_1), .Output_bus_1(Compliment_1_output_bus_1));
  IP IP_1 (.Input_bus_1(Compliment_1_output_bus_1), .Output_bus_1({IP_1_output_bus_1, IP_1_output_bus_1_2}));
  Compliment_10 Compliment_10_1 (
    .Input_bus_1(Input_bus_2),
    .Output_bus_1({Compliment_10_1_output_bus_1_2[0], Compliment_10_1_output_bus_1_2[2], Compliment_10_1_output_bus_1_2[6], Compliment_10_1_output_bus_1[6], Compliment_10_1_output_bus_1_2[4], Compliment_10_1_output_bus_1_2[5], Compliment_10_1_output_bus_1[3], Compliment_10_1_output_bus_1_2[7], Compliment_10_1_output_bus_1_2[1], Compliment_10_1_output_bus_1_2[3]}));
  EP EP_2 (
    .Input_1(IP_1_output_bus_1_2[0]), .Input_2(IP_1_output_bus_1_2[1]), .Input_3(IP_1_output_bus_1_2[2]),
    .Input_4(IP_1_output_bus_1_2[3]), .Output_bus_1(EP_2_output_bus_1));
  assign xor_1_out = EP_2_output_bus_1 ^ {Compliment_10_1_output_bus_1_2[0], Compliment_10_1_output_bus_1[3], Compliment_10_1_output_bus_1_2[1], Compliment_10_1_output_bus_1[6], Compliment_10_1_output_bus_1_2[7:6], Compliment_10_1_output_bus_1_2[3], Compliment_10_1_output_bus_1_2[5]};  // XOR_Gate xor_1, 8 bits wide
  S1 S1_2 (.Input_bus_1(xor_1_out[3:0]), .Output_bus_1(S1_2_output_bus_1));
  S0 S0_2 (.Input_bus_1(xor_1_out[7:4]), .Output_bus_1(S0_2_output_bus_1));
  P4 P4_2 (.Input_bus_1({S0_2_output_bus_1, S1_2_output_bus_1}), .Output_bus_1(P4_2_output_bus_1));
  assign xor_2_out = P4_2_output_bus_1 ^ IP_1_output_bus_1;  // XOR_Gate xor_2, 4 bits wide
  assign xor_3_out = EP_1_output_bus_1 ^ Compliment_10_1_output_bus_1_2;  // XOR_Gate xor_3, 8 bits wide
  EP EP_1 (
    .Input_1(xor_2_out[0]), .Input_2(xor_2_out[1]), .Input_3(xor_2_out[2]), .Input_4(xor_2_out[3]),
    .Output_bus_1(EP_1_output_bus_1));
  S1 S1_1 (.Input_bus_1(xor_3_out[3:0]), .Output_bus_1(S1_1_output_bus_1));
  S0 S0_1 (.Input_bus_1(xor_3_out[7:4]), .Output_bus_1(S0_1_output_bus_1));
  P4 P4_1 (.Input_bus_1({S0_1_output_bus_1, S1_1_output_bus_1}), .Output_bus_1(P4_1_output_bus_1));
  assign xor_4_out = P4_1_output_bus_1 ^ IP_1_output_bus_1_2;  // XOR_Gate xor_4, 4 bits wide
  IP_inv IP_inv_1 (.Input_bus_1({xor_4_out, xor_2_out}), .Output_bus_1(IP_inv_1_output_bus_1));
  Compliment Compliment_2 (.Input_bus_1(IP_inv_1_output_bus_1), .Output_bus_1(Output_bus_2));
endmodule

module DFF_8 (
  input  [7:0] in_1,
  input  in_2,
  input  in_3,
  output [7:0] out_4
);

  D_Flip_Flop d_ff_1 (.clk(in_2), .D(in_1[7]), .Q(out_4[7]), .reset(in_3));  // open: Qn, preset
  D_Flip_Flop d_ff_2 (.clk(in_2), .D(in_1[6]), .Q(out_4[6]), .reset(in_3));  // open: Qn, preset
  D_Flip_Flop d_ff_3 (.clk(in_2), .D(in_1[5]), .Q(out_4[5]), .reset(in_3));  // open: Qn, preset
  D_Flip_Flop d_ff_4 (.clk(in_2), .D(in_1[4]), .Q(out_4[4]), .reset(in_3));  // open: Qn, preset
  D_Flip_Flop d_ff_5 (.clk(in_2), .D(in_1[3]), .Q(out_4[3]), .reset(in_3));  // open: Qn, preset
  D_Flip_Flop d_ff_6 (.clk(in_2), .D(in_1[2]), .Q(out_4[2]), .reset(in_3));  // open: Qn, preset
  D_Flip_Flop d_ff_7 (.clk(in_2), .D(in_1[1]), .Q(out_4[1]), .reset(in_3));  // open: Qn, preset
  D_Flip_Flop d_ff_8 (.clk(in_2), .D(in_1[0]), .Q(out_4[0]), .reset(in_3));  // open: Qn, preset
endmodule

module or_8 (
  input  [7:0] in_1,
  output out_2
);

  or or_1 (out_2, in_1[0], in_1[1], in_1[2], in_1[3], in_1[4], in_1[5], in_1[6], in_1[7]);
endmodule
